// Digital circuit custom.dig as structural Verilog
module custom (
  input  A,
  input  B,
  input  C,
  output Y
);

  wire and_1_out, not_1_out;

  not not_1 (not_1_out, C);
  and and_1 (and_1_out, A, B);
  or or_1 (Y, and_1_out, not_1_out);
endmodule
